// Digital circuit counter4test.dig as structural Verilog
module counter4test (
  input  clk,
  input  in_2,
  input  in_3,
  input  in_4,
  input  in_5,
  output out_6,
  output out_7
);

  wire [3:0] upcounter_1_p4;

  // upcounter upcounter_1: pin names not known; wires that end beside it: in_3, in_2, clk, upcounter_1_p4
  T_FF t_ff_1 (.T(in_4), .C(in_5), .Q(out_6), .nQ(out_7));
  Seven_Seg_Hex seven_seg_hex_1 (.d(upcounter_1_p4), .dp(1'b0));
endmodule
