// Digital circuit upcounter.dig as structural Verilog
module upcounter (
  input  EN,
  input  CLK,
  output [3:0] CNT
);

  wire and_1_out, and_2_out, and_3_out, and_4_out, and_5_out, and_9_out, d_ff_1_q, d_ff_as_1_nq,
       d_ff_as_2_nq, d_ff_as_3_nq, d_ff_as_4_nq, multiplexer_1_out, multiplexer_2_out, multiplexer_3_out,
       multiplexer_4_out, not_1_out, not_2_out, t_ff_1_q;
  wire [0:0] and_6_out, and_7_out;
  wire [1:0] and_8_out;

  and and_1 (and_1_out, EN, not_1_out);
  and and_2 (and_2_out, CLK, and_1_out);
  D_FF d_ff_1 (.D(1'b1), .C(and_2_out), .Q(d_ff_1_q));  // open: nQ
  not not_1 (not_1_out, CLK);
  and and_3 (and_3_out, EN, and_9_out);
  not not_2 (not_2_out, d_ff_1_q);
  and and_4 (and_4_out, EN, not_2_out);
  T_FF t_ff_1 (.T(and_3_out), .C(CLK), .Q(t_ff_1_q));  // open: nQ
  or or_1 (and_8_out[1], and_5_out, and_4_out);
  and and_5 (and_5_out, EN, t_ff_1_q);
  and and_6 (and_6_out[0], CNT[0], EN);
  and and_7 (and_7_out[0], CNT[1], and_6_out[0]);
  and and_8 (and_8_out[0], CNT[2], and_7_out[0]);
  Multiplexer #(.Selector_Bits(2)) multiplexer_1 (
    .sel({and_8_out[1], EN}), .in_0(CNT[0]), .in_1(d_ff_as_1_nq), .in_2(1'b0), .in_3(1'b0),
    .out(multiplexer_1_out));
  Multiplexer #(.Selector_Bits(2)) multiplexer_2 (
    .sel({and_8_out[1], and_6_out[0]}), .in_0(CNT[1]), .in_1(d_ff_as_2_nq), .in_2(1'b1), .in_3(1'b1),
    .out(multiplexer_2_out));
  Multiplexer #(.Selector_Bits(2)) multiplexer_3 (
    .sel({and_8_out[1], and_7_out[0]}), .in_0(CNT[2]), .in_1(d_ff_as_3_nq), .in_2(1'b0), .in_3(1'b0),
    .out(multiplexer_3_out));
  Multiplexer #(.Selector_Bits(2)) multiplexer_4 (
    .sel(and_8_out), .in_0(CNT[3]), .in_1(d_ff_as_4_nq), .in_2(1'b0), .in_3(1'b0), .out(multiplexer_4_out));
  D_FF_AS d_ff_as_1 (.Set(1'b0), .D(multiplexer_1_out), .C(CLK), .Clr(1'b0), .Q(CNT[0]), .nQ(d_ff_as_1_nq));
  D_FF_AS d_ff_as_2 (.Set(1'b0), .D(multiplexer_2_out), .C(CLK), .Clr(1'b0), .Q(CNT[1]), .nQ(d_ff_as_2_nq));
  D_FF_AS d_ff_as_3 (.Set(1'b0), .D(multiplexer_3_out), .C(CLK), .Clr(1'b0), .Q(CNT[2]), .nQ(d_ff_as_3_nq));
  D_FF_AS d_ff_as_4 (.Set(1'b0), .D(multiplexer_4_out), .C(CLK), .Clr(1'b0), .Q(CNT[3]), .nQ(d_ff_as_4_nq));
  and and_9 (and_9_out, CNT[3], CNT[1]);
endmodule
