// Digital circuit statemachine.dig as structural Verilog
module statemachine (
  input  A,
  input  B,
  input  CLK,
  output OUT
);

  wire delay_1_out;

  Delay delay_1 (.in(B), .out(delay_1_out));
  and and_1 (OUT, A, delay_1_out, CLK);
endmodule
