// Digital circuit bin to glixon.dig as structural Verilog
module bin_to_glixon (
  input  in_1,
  input  in_2,
  input  in_3,
  input  in_4,
  output out_5,
  output out_6,
  output out_7,
  output out_8
);

  wire and_2_out, and_3_out, and_4_out, and_5_out, and_6_out, and_7_out, not_1_out, not_2_out, not_3_out,
       not_4_out, or_2_out, or_3_out;

  not not_1 (not_1_out, in_1);
  not not_2 (not_2_out, in_2);
  not not_3 (not_3_out, in_3);
  not not_4 (not_4_out, in_4);
  and and_1 (out_5, in_1, not_2_out, not_3_out);
  and and_2 (and_2_out, not_1_out, in_2);
  and and_3 (and_3_out, in_1, not_2_out, not_3_out, not_4_out);
  and and_4 (and_4_out, in_2, not_3_out);
  and and_5 (and_5_out, in_3, not_2_out);
  and and_6 (and_6_out, not_3_out, in_4);
  and and_7 (and_7_out, in_3, not_4_out);
  or or_1 (out_6, and_2_out, and_3_out);
  or or_2 (or_2_out, and_4_out, and_5_out);
  or or_3 (or_3_out, and_6_out, and_7_out);
  and and_8 (out_7, or_2_out, not_1_out);
  and and_9 (out_8, or_3_out, not_1_out);
endmodule
