// Digital circuit hw3q4.dig as structural Verilog
module hw3q4 (
  input  a,
  input  b,
  input  c,
  output sum,
  output carry
);

  wire not_1_out;

  not not_1 (not_1_out, a);
  Multiplexer #(.Selector_Bits(2)) multiplexer_1 (
    .sel({c, b}), .in_0(a), .in_1(not_1_out), .in_2(not_1_out), .in_3(a), .out(sum));
  Multiplexer #(.Selector_Bits(2)) multiplexer_2 (
    .sel({c, b}), .in_0(1'b0), .in_1(a), .in_2(a), .in_3(1'b1), .out(carry));
endmodule
