// Digital circuit lab1f.dig as structural Verilog
module lab1f (
  input  in_1,
  input  in_2,
  input  in_3,
  input  in_4,
  input  in_5,
  input  in_6,
  input  in_7,
  input  in_8
);

  wire abs_1_p1, abs_1_p3;
  wire [3:0] add_1_s, unsignedbcd6_1_p1, unsignedbcd6_1_p3, unsignedbcd_1_p1, unsignedbcd_1_p3,
       unsignedbcd_2_p1, unsignedbcd_2_p3;
  wire [4:4] add_1_c_o;
  wire [5:0] abs_1_p2, add_2_s, not_1_out;

  Seven_Seg_Hex seven_seg_hex_1 (.d(unsignedbcd_1_p1), .dp(1'b0));
  Seven_Seg_Hex seven_seg_hex_2 (.d(unsignedbcd_1_p3), .dp(1'b0));
  // unsignedBCD unsignedbcd_1: pin names not known; wires that end beside it: unsignedbcd_1_p1, {in_5, in_6, in_7, in_8}, unsignedbcd_1_p3
  Add #(.Bits(4)) add_1 (
    .a({in_5, in_6, in_7, in_8}), .b({in_5, in_6, in_7, in_8}), .c_i(1'b0), .s(add_1_s), .c_o(add_1_c_o[4]));
  Seven_Seg_Hex seven_seg_hex_3 (.d(unsignedbcd_2_p1), .dp(1'b0));
  Seven_Seg_Hex seven_seg_hex_4 (.d(unsignedbcd_2_p3), .dp(1'b0));
  // unsignedBCD unsignedbcd_2: pin names not known; wires that end beside it: unsignedbcd_2_p1, {in_1, in_2, in_3, in_4}, unsignedbcd_2_p3
  assign not_1_out = ~{2'b00, in_1, in_2, in_3, in_4};  // Not not_1, 6 bits wide
  Seven_Seg seven_seg_1 (.a(1'b0), .b(1'b0), .c(1'b0), .d(1'b0), .e(1'b0), .f(1'b0), .g(abs_1_p1), .dp(1'b0));
  Add #(.Bits(6)) add_2 (.a(not_1_out), .b(6'b000001), .c_i(1'b0), .s(add_2_s));  // open: c_o
  Seven_Seg_Hex seven_seg_hex_5 (.d(unsignedbcd6_1_p1), .dp(1'b0));
  // abs abs_1: pin names not known; wires that end beside it: abs_1_p1, abs_1_p2, abs_1_p3
  Seven_Seg_Hex seven_seg_hex_6 (.d(unsignedbcd6_1_p3), .dp(1'b0));
  Add #(.Bits(6)) add_3 (.a({1'b0, add_1_c_o[4], add_1_s}), .b(add_2_s), .c_i(1'b0), .s(abs_1_p2));  // open: c_o
  // unsignedBCD6 unsignedbcd6_1: pin names not known; wires that end beside it: unsignedbcd6_1_p1, abs_1_p3, unsignedbcd6_1_p3

  // Notes on the sheet:
  //   2x
  //   _
  //   =
endmodule
