// Digital circuit prelab4.dig as structural Verilog
module prelab4 (
  input  in_1,
  input  clk
);

  wire and_1_out, and_2_out, and_3_out, and_4_out, and_5_out, and_6_out, cntdecud_2_p6, cntdecud_2_p7,
       d_ff_1_q, d_ff_2_q, d_ff_3_q, d_ff_4_q, d_ff_5_q, d_ff_6_q, d_ff_7_q, d_ff_8_q, d_ff_9_q, d_ff_10_q,
       d_ff_11_q, d_ff_12_q, d_ff_13_q, d_ff_14_q, d_ff_15_q, d_ff_16_q, down_out, not_1_out, not_2_out,
       or_1_out, or_2_out, up_out;
  wire [3:0] cntdecud_1_p5, cntdecud_2_p5;

  Button up (.out(up_out));
  Button down (.out(down_out));
  and and_1 (and_1_out, and_3_out, d_ff_15_q);
  D_FF d_ff_1 (.D(and_1_out), .C(clk), .Q(d_ff_1_q));  // open: nQ
  D_FF d_ff_2 (.D(and_2_out), .C(clk), .Q(d_ff_2_q));  // open: nQ
  and and_2 (and_2_out, and_4_out, d_ff_16_q);
  or or_1 (or_1_out, up_out, d_ff_1_q);
  or or_2 (or_2_out, down_out, d_ff_2_q);
  D_FF d_ff_3 (.D(or_1_out), .C(clk), .Q(d_ff_3_q));  // open: nQ
  D_FF d_ff_4 (.D(or_2_out), .C(clk), .Q(d_ff_4_q));  // open: nQ
  D_FF d_ff_5 (.D(d_ff_3_q), .C(clk), .Q(d_ff_5_q));  // open: nQ
  not not_1 (not_1_out, or_1_out);
  D_FF d_ff_6 (.D(or_1_out), .C(clk), .Q(d_ff_6_q));  // open: nQ
  not not_2 (not_2_out, or_2_out);
  D_FF d_ff_7 (.D(or_2_out), .C(clk), .Q(d_ff_7_q));  // open: nQ
  D_FF d_ff_8 (.D(d_ff_4_q), .C(clk), .Q(d_ff_8_q));  // open: nQ
  D_FF d_ff_9 (.D(d_ff_5_q), .C(clk), .Q(d_ff_9_q));  // open: nQ
  D_FF d_ff_10 (.D(d_ff_8_q), .C(clk), .Q(d_ff_10_q));  // open: nQ
  D_FF d_ff_11 (.D(d_ff_9_q), .C(clk), .Q(d_ff_11_q));  // open: nQ
  D_FF d_ff_12 (.D(d_ff_10_q), .C(clk), .Q(d_ff_12_q));  // open: nQ
  D_FF d_ff_13 (.D(d_ff_11_q), .C(clk), .Q(d_ff_13_q));  // open: nQ
  and and_3 (and_3_out, not_1_out, d_ff_6_q);
  and and_4 (and_4_out, not_2_out, d_ff_7_q);
  D_FF d_ff_14 (.D(d_ff_12_q), .C(clk), .Q(d_ff_14_q));  // open: nQ
  D_FF d_ff_15 (.D(d_ff_13_q), .C(clk), .Q(d_ff_15_q));  // open: nQ
  D_FF d_ff_16 (.D(d_ff_14_q), .C(clk), .Q(d_ff_16_q));  // open: nQ
  and and_5 (and_5_out, cntdecud_2_p7, and_3_out);
  and and_6 (and_6_out, cntdecud_2_p6, and_4_out);
  // cntDECud cntdecud_1: pin names not known; wires that end beside it: and_5_out, and_6_out, clk, in_1, cntdecud_1_p5
  Seven_Seg_Hex seven_seg_hex_1 (.d(cntdecud_1_p5), .dp(1'b0));
  Seven_Seg_Hex seven_seg_hex_2 (.d(cntdecud_2_p5), .dp(1'b0));
  // cntDECud cntdecud_2: pin names not known; wires that end beside it: and_3_out, and_4_out, clk, in_1, cntdecud_2_p5, cntdecud_2_p6, cntdecud_2_p7

  // Notes on the sheet:
  //   clk: Hz: 100
endmodule
