// Digital circuit mode_selector.dig as structural Verilog
module mode_selector (
  input  ID,
  input  PWD,
  input  DIS,
  input  RESET,
  input  CLK,
  input  RST,
  output IDO,
  output PWDO
);

  wire and_1_out, and_2_out, and_3_out, and_4_out, not_1_out, not_2_out, not_3_out, or_1_out, or_2_out;

  not not_1 (not_1_out, DIS);
  and and_1 (and_1_out, ID, RST, not_1_out);
  and and_2 (and_2_out, PWD, RST, not_2_out);
  not not_2 (not_2_out, DIS);
  and and_3 (and_3_out, CLK, PWDO);
  or or_1 (or_1_out, and_1_out, RESET);
  not not_3 (not_3_out, or_1_out);
  and and_4 (and_4_out, RESET, and_3_out);
  D_FF d_ff_1 (.D(not_3_out), .C(or_2_out), .Q(PWDO), .nQ(IDO));
  or or_2 (or_2_out, and_2_out, and_4_out);
endmodule
