// Digital circuit shifter.dig as structural Verilog
module shifter (
  input  [3:0] IN,
  input  EN,
  input  DA,
  input  CLK,
  input  RST,
  output [3:0] ID1,
  output [3:0] ID0,
  output [6:0] HEX
);

  wire and_1_out, and_2_out, and_3_out, and_4_out, d_ff_1_q, not_1_out;
  wire [7:0] mul_1_mul;
  wire [7:7] add_1_s;

  and and_1 (and_1_out, RST, EN);
  and and_2 (and_2_out, and_1_out, DA);
  and and_3 (and_3_out, CLK, and_1_out);
  not not_1 (not_1_out, and_2_out);
  D_FF d_ff_1 (.D(and_2_out), .C(and_3_out), .Q(d_ff_1_q));  // open: nQ
  D_FF #(.Bits(4)) d_ff_2 (.D(IN), .C(and_4_out), .Q(ID0));  // open: nQ
  and and_4 (and_4_out, not_1_out, d_ff_1_q);
  D_FF #(.Bits(4)) d_ff_3 (.D(ID0), .C(and_4_out), .Q(ID1));  // open: nQ
  Mul #(.Bits(4)) mul_1 (.a(ID1), .b(4'b1010), .mul(mul_1_mul));
  Add #(.Bits(8)) add_1 (.a({4'b0000, ID0}), .b(mul_1_mul), .c_i(1'b0), .s({add_1_s[7], HEX}));  // open: c_o
endmodule
