// Digital circuit shifter_pwd.dig as structural Verilog
module shifter_pwd (
  input  [3:0] DATA_in,
  input  [15:0] PWD_in,
  input  EN,
  input  DA,
  input  CLK,
  input  RST,
  output MATCH,
  output LED1,
  output LED2,
  output LED3,
  output LED4
);

  wire add_2_c_o, and_1_out, and_2_out, and_3_out, and_8_out, d_ff_1_q, d_ff_3_q, d_ff_4_q, d_ff_5_q,
       d_ff_6_q, d_ff_7_q, not_1_out, not_2_out, or_1_out, or_2_out, xnor_1_out, xnor_2_out, xnor_3_out,
       xnor_4_out;
  wire [0:0] d_ff_2_q;
  wire [1:0] add_1_s, add_2_s;
  wire [3:0] multiplexer_1_out;

  not not_1 (not_1_out, EN);
  and and_1 (and_1_out, EN, EN, RST);
  and and_2 (and_2_out, not_1_out, CLK);
  D_FF d_ff_1 (.D(and_1_out), .C(or_1_out), .Q(d_ff_1_q));  // open: nQ
  or or_1 (or_1_out, DA, and_2_out);
  D_FF d_ff_2 (.D(d_ff_1_q), .C(or_1_out), .Q(d_ff_2_q[0]));  // open: nQ
  D_FF d_ff_3 (.D(d_ff_2_q[0]), .C(or_1_out), .Q(d_ff_3_q));  // open: nQ
  D_FF d_ff_4 (.D(d_ff_3_q), .C(or_1_out), .Q(d_ff_4_q));  // open: nQ
  Add add_1 (.a(d_ff_4_q), .b(d_ff_3_q), .c_i(1'b0), .s(add_1_s[0]), .c_o(add_1_s[1]));
  Add #(.Bits(2)) add_2 (.a(add_1_s), .b({1'b0, d_ff_2_q[0]}), .c_i(1'b0), .s(add_2_s), .c_o(add_2_c_o));
  Multiplexer #(.Bits(4), .Selector_Bits(2)) multiplexer_1 (
    .sel(add_2_s), .in_0(PWD_in[15:12]), .in_1(PWD_in[11:8]), .in_2(PWD_in[7:4]), .in_3(PWD_in[3:0]),
    .out(multiplexer_1_out));
  xnor xnor_1 (xnor_1_out, DATA_in[0], multiplexer_1_out[0]);
  xnor xnor_2 (xnor_2_out, DATA_in[1], multiplexer_1_out[1]);
  xnor xnor_3 (xnor_3_out, DATA_in[2], multiplexer_1_out[2]);
  xnor xnor_4 (xnor_4_out, DATA_in[3], multiplexer_1_out[3]);
  and and_3 (and_3_out, xnor_1_out, xnor_2_out, xnor_3_out, xnor_4_out);
  and and_4 (LED1, d_ff_1_q, EN);
  and and_5 (LED2, d_ff_2_q[0], EN);
  and and_6 (LED3, d_ff_3_q, EN);
  and and_7 (LED4, d_ff_4_q, EN);
  and and_8 (and_8_out, CLK, not_2_out);
  not not_2 (not_2_out, EN);
  or or_2 (or_2_out, and_3_out, and_8_out);
  D_FF d_ff_5 (.D(EN), .C(or_2_out), .Q(d_ff_5_q));  // open: nQ
  D_FF d_ff_6 (.D(d_ff_5_q), .C(or_2_out), .Q(d_ff_6_q));  // open: nQ
  D_FF d_ff_7 (.D(d_ff_6_q), .C(or_2_out), .Q(d_ff_7_q));  // open: nQ
  D_FF d_ff_8 (.D(d_ff_7_q), .C(or_2_out), .Q(MATCH));  // open: nQ
endmodule
