// Digital circuit timer.dig as structural Verilog
module timer (
  input  START,
  input  CLK,
  input  RST,
  output RESET,
  output DIS
);

  wire and_1_out, and_2_out, d_ff_1_nq, d_ff_2_nq, not_1_out, or_1_out;

  and and_1 (and_1_out, CLK, START, RST);
  and and_2 (and_2_out, not_1_out, CLK);
  not not_1 (not_1_out, START);
  D_FF d_ff_1 (.D(START), .C(and_1_out), .nQ(d_ff_1_nq));  // open: Q
  CounterPreset #(.Bits(9)) counterpreset_1 (
    .en(START), .C(and_1_out), .dir(1'b0), .in(9'hd4), .ld(d_ff_1_nq), .clr(RESET), .ovf(RESET));  // open: out
  or or_1 (or_1_out, RESET, and_2_out);
  D_FF d_ff_2 (.D(START), .C(or_1_out), .nQ(d_ff_2_nq));  // open: Q
  and and_3 (DIS, START, RST, d_ff_2_nq);
endmodule
